# Fritzing sketch circuito (saved by Fritzing 1.0.1rc)
breadboards: 1

parts:
  M1 = DOIT Esp32 DevKit v1 (30 pins long, 11 pins width) [part_number=ESP32S-PIN30]
  R1 = Resistor [tolerance=±5% power=0.25 resistance=220 package=THT]
  Motor = LED - 5mm [color="Red (633nm)" current=0.030 package="5 mm [THT]"]
  liga = Pushbutton [package="[THT]"]
  desliga = Pushbutton [package="[THT]"]
  R2 = Resistor [tolerance=±5% power=0.25 resistance=10k package=THT]
  R3 = Resistor [tolerance=±5% power=0.25 resistance=10k package=THT]

nets:
  N1: M1.3V3, liga.Pin_1, liga.Pin_2, desliga.Pin_1, desliga.Pin_2
  N2: M1.GND, Motor.cathode, R2.Pin_1, R3.Pin_1
  N3: M1.D15, R1.Pin_0
  N4: M1.D22, desliga.Pin_3, desliga.Pin_4, R3.Pin_0
  N5: M1.D23, liga.Pin_3, liga.Pin_4, R2.Pin_0
  N6: R1.Pin_1, Motor.anode

custom parts:
  DOIT Esp32 DevKit v1 (30 pins long, 11 pins width): The DOIT Esp32 DevKit v1 is one of the development board created by DOIT to evaluate the ESP-WROOM-32 module. It is based on the ESP32 microcontroller that boasts Wifi, Bluetooth, Ethernet and Low Power support all in a single chip. (vanepp) made breadboard work, adjusted pin numbering and labels and reduced size of schematic and cleaned up pcb. This chip is 30pins long (2 x15) and 11 pins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
