# Fritzing sketch circuito_analogica (saved by Fritzing 1.0.1rc)
breadboards: 1

parts:
  M1 = DOIT Esp32 DevKit v1 (30 pins long, 11 pins width) [part_number=ESP32S-PIN30]
  U1 = POT [knob_status=50% package=pot_mammoth]
  LED1 = LED - 5mm [color="Red (633nm)" current=0.030 package="5 mm [THT]"]
  R1 = Resistor [tolerance=±5% resistance=220 package="2512 [SMD]"]

nets:
  N1: M1.3V3, U1.S
  N2: M1.GND, U1.E, LED1.cathode
  N3: M1.D34, U1.A
  N4: M1.D25, R1.Pin_1
  N5: LED1.anode, R1.Pin_0

custom parts:
  DOIT Esp32 DevKit v1 (30 pins long, 11 pins width): The DOIT Esp32 DevKit v1 is one of the development board created by DOIT to evaluate the ESP-WROOM-32 module. It is based on the ESP32 microcontroller that boasts Wifi, Bluetooth, Ethernet and Low Power support all in a single chip. (vanepp) made breadboard work, adjusted pin numbering and labels and reduced size of schematic and cleaned up pcb. This chip is 30pins long (2 x15) and 11 pins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
